# Fritzing sketch shemaPCB (saved by Fritzing 0.9.2b)
circuit board: 5.42266cm x 5.99977cm
breadboards: 1

parts:
  VCC1 = Battery block 9V
  KEYPAD1 = Membrane Matrix Keypad
  R1 = Resistor [tolerance=±5% resistance=220 package=THT]
  R3 = Resistor [tolerance=±5% resistance=220 package=THT]
  R4 = Resistor [tolerance=±5% resistance=220 package=THT]
  LED1 = 7-SEGMENT-4DIGIT-YOUNGSUN [package=7-segment-4digit-youngsun]
  R2 = Resistor [tolerance=±5% resistance=220 package=THT]
  Part1 = Arduino Nano (Rev3.0)
  J1 = Basic Servo

nets:
  GND: VCC1.-, Part1.GND, J1.gnd
  N1: VCC1.+, Part1.VIN
  N2: KEYPAD1.1, Part1.D12/MISO
  N3: KEYPAD1.2, Part1.D11/MOSI
  N4: KEYPAD1.3, Part1.D10
  N5: KEYPAD1.4, Part1.D9
  N6: KEYPAD1.5, Part1.D8
  N7: KEYPAD1.6, Part1.D7
  N8: KEYPAD1.7, Part1.D6
  N9: R1.Pin_0, Part1.D5
  N10: R1.Pin_1, LED1.G
  N11: R3.Pin_0, Part1.D1/TX
  N12: R3.Pin_1, LED1.F
  N13: R4.Pin_0, LED1.DP
  N14: R4.Pin_1, Part1.A0
  N15: LED1.DIG2, Part1.A5
  N16: LED1.D, Part1.A4
  N17: LED1.COL-A, Part1.A3
  N18: LED1.E, Part1.A2
  N19: LED1.DIG3, Part1.A1
  N20: LED1.APOS-A, Part1.D0/RX
  N21: LED1.COL-C, R2.Pin_1
  N22: LED1.C, Part1.D3
  N23: LED1.A, Part1.D4
  N24: R2.Pin_0, Part1.D2
  5V: Part1.5V, J1.vcc
  N25: Part1.D13/SCK, J1.pulse

custom parts:
  Membrane Matrix Keypad: Membrane Matrix 3x4 Keypad
